# Fritzing sketch NanoPCB (saved by Fritzing 0.9.3b)
circuit board: 6.6cm x 6.1cm
breadboards: 1

parts:
  Arduino_nano = Arduino Nano (Rev3.0)
  S1 = Dagu DGServo 9g header (male) [package=THT]
  S2 = Dagu DGServo 9g header (male) [package=THT]
  S3 = Dagu DGServo 9g header (male) [package=THT]
  S4 = Dagu DGServo 9g header (male) [package=THT]
  Relays = female pin header, 6 pins [form="♀ (female)"]
  +5V = Camdenboss CTB0158-2 [part_number=CTB0158-2 package=THT]
  R1 = Resistor [tolerance=±5% resistance=220 package="0805 [SMD]"]
  D1 = LTE-302 [package=lte-302]
  part = Pad [width=3 height=5 connect=center]
  Pad4 = Pad [width=3 height=5 connect=center]
  Pad6 = Pad [width=3 height=5 connect=center]
  Pad8 = Pad [width=3 height=5 connect=center]
  Pad9 = Pad [width=3 height=5 connect=center]
  Pad10 = Pad [width=3 height=5 connect=center]
  Pad11 = Pad [width=3 height=5 connect=center]
  Pad2 = Pad [width=3 height=5 connect=center]

nets:
  GND: Arduino_nano.GND, S1.gnd, S2.gnd, S3.gnd, S4.gnd, Relays.pin1, +5V.pin2, D1.C, Pad8.pad, Pad9.pad, Pad10.pad, Pad11.pad
  N1: Arduino_nano.D5, R1.Pin_1
  N2: Arduino_nano.D9, Relays.pin3
  N3: Arduino_nano.D10, Relays.pin4
  N4: Arduino_nano.D11/MOSI, Relays.pin5
  N5: Arduino_nano.D12/MISO, Relays.pin6
  N6: Arduino_nano.VIN, +5V.pin1, part.pad, Pad4.pad, Pad6.pad, Pad2.pad
  VCC: Arduino_nano.5V, S1.Vcc, S2.Vcc, S3.Vcc, S4.Vcc, Relays.pin2
  N7: Arduino_nano.A3, S1.pulse
  N8: Arduino_nano.A2, S2.pulse
  N9: Arduino_nano.A1, S3.pulse
  N10: Arduino_nano.A0, S4.pulse
  N11: R1.Pin_0, D1.A

notes:
  Pumps +
  Pumps -
